# Fritzing sketch Schema (saved by Fritzing 0.9.3b)
breadboards: 1

parts:
  R2 = Resistor [tolerance=±5% resistance=240k package=THT]
  R1 = Resistor [tolerance=±5% resistance=10k package=THT]
  U1 = AD8226 - Rail-to-Rail output Instrumentation Amplifier [part_number=AD8226]
  U2 = OPA344 [package=sot23-5]

nets:
  N1: R2.Pin_0, R1.Pin_1, U2.+IN
  N2: R2.Pin_1, U1.-IN, U2.OUT
  GND: R1.Pin_0, U2.V-
  -15V: U1.-VS
  15V: U1.+VS, U2.V+
  0.4V: U2.-IN
